# Fritzing sketch Schéma ESP32 (saved by Fritzing 0.9.3b)
breadboards: 1

parts:
  Gyroscope_accéléromètre = InvenSense MPU6050
  Afficheur_4x7_segments = Grove 4 Digit Display
  Servo-moteur = Basic Servo
  U1 = ESP32-38PinWide [part_number=ESP32-38PinWide]
  VCC1 = 4 x AAA Battery Mount

nets:
  VCC: Gyroscope_accéléromètre.VCC, Afficheur_4x7_segments.VCC, Servo-moteur.vcc, VCC1.+
  GND: Gyroscope_accéléromètre.GND, Afficheur_4x7_segments.GND, Servo-moteur.gnd, VCC1.-
  N1: Gyroscope_accéléromètre.SCL, U1.GPIO22
  N2: Gyroscope_accéléromètre.SDA, U1.GPIO21
  N3: Afficheur_4x7_segments.DIO, U1.GPIO4
  N4: Afficheur_4x7_segments.CLK, U1.GPIO2
  N5: Servo-moteur.pulse, U1.GPIO23

custom parts:
  ESP32-38PinWide: Generic 38-Pin ESP32 with wide format (only access to one side of pins on a breadboard) based on Stephen Lilley's HiLetgo ESP-WROOM-32 ESP32 ESP-32S Development Board.
